// Logisim project inizio.circ as structural Verilog: 1 circuit, main circuit main
module main (
  input  [1:0] PLAYER1,
  input  [1:0] PLAYER2,
  input  START,
  output [1:0] out_4,
  output [1:0] out_5,
  output [4:0] out_6
);

  wire clock_1_out;
  wire [1:0] demultiplexer_1_out1, demultiplexer_2_out1;
  wire [4:0] adder_1_out, adder_2_out, multiplexer_1_out, multiplexer_2_out;

  Demultiplexer #(.width(2)) demultiplexer_1 (.out0(out_4), .out1(demultiplexer_1_out1), .in(PLAYER1), .sel(START));
  Demultiplexer #(.width(2)) demultiplexer_2 (.out0(out_5), .out1(demultiplexer_2_out1), .in(PLAYER2), .sel(START));
  Multiplexer #(.select(2), .width(5)) multiplexer_1 (
    .in0({5{1'b0}}), .in1(5'b00100), .in2(5'b01000), .in3(5'b01100), .out(multiplexer_1_out),
    .sel(demultiplexer_1_out1));
  Clock clock_1 (.out(clock_1_out));
  Multiplexer #(.select(2), .width(5)) multiplexer_2 (
    .in0({5{1'b0}}), .in1(5'b00001), .in2(5'b00010), .in3(5'b00011), .out(multiplexer_2_out),
    .sel(demultiplexer_2_out1));
  Adder #(.width(5)) adder_1 (.a(multiplexer_2_out), .b(multiplexer_1_out), .out(adder_1_out));  // open: cin, cout
  Adder #(.width(5)) adder_2 (.a(adder_1_out), .b(5'b00100), .out(adder_2_out));  // open: cin, cout
  Register #(.width(5)) MAX_MANCHE (.D(adder_2_out), .Q(out_6), .clk(clock_1_out));  // open: en, clr
endmodule
