// Logisim project logica_gestione_partita.circ as structural Verilog: 1 circuit, main circuit main
module main (
  input  [1:0] OUTPUT_LOGICA_PERSONALIZZATA,
  input  START
);

  wire clock_1_out, comparator_1_gt, comparator_2_eq, comparator_3_eq, nor_1_out;
  wire [4:0] adder_1_out, adder_2_out, ADVANTAGE_REGISTER_q, MANCHE_COUNT_q, multiplexer_1_out,
       multiplexer_2_out, multiplexer_3_out, multiplexer_4_out, multiplexer_5_out, subtractor_1_out;

  Comparator #(.mode("unsigned"), .width(2)) comparator_1 (
    .a(OUTPUT_LOGICA_PERSONALIZZATA), .b(2'b00), .gt(comparator_1_gt));  // open: eq, lt
  Comparator #(.mode("unsigned"), .width(2)) comparator_2 (
    .a(OUTPUT_LOGICA_PERSONALIZZATA), .b(2'b00), .eq(comparator_2_eq));  // open: gt, lt
  Comparator #(.mode("unsigned"), .width(2)) comparator_3 (
    .a(OUTPUT_LOGICA_PERSONALIZZATA), .b(2'b11), .eq(comparator_3_eq));  // open: gt, lt
  nor nor_1 (nor_1_out, comparator_2_eq, comparator_3_eq);
  Adder #(.width(5)) adder_1 (.a(multiplexer_1_out), .b(ADVANTAGE_REGISTER_q), .out(adder_1_out));  // open: cin, cout
  Subtractor #(.width(5)) subtractor_1 (
    .a(ADVANTAGE_REGISTER_q), .b(multiplexer_1_out), .out(subtractor_1_out));  // open: bin, bout
  Multiplexer #(.width(5)) multiplexer_1 (.in0({5{1'b0}}), .in1(5'b00001), .out(multiplexer_1_out), .sel(nor_1_out));
  Multiplexer #(.select(2), .width(5)) multiplexer_2 (
    .in0(ADVANTAGE_REGISTER_q), .in1(subtractor_1_out), .in2(adder_1_out), .in3(ADVANTAGE_REGISTER_q),
    .out(multiplexer_2_out), .sel(OUTPUT_LOGICA_PERSONALIZZATA));
  Multiplexer #(.width(5)) multiplexer_3 (
    .in0(multiplexer_2_out), .in1(5'b00010), .out(multiplexer_3_out), .sel(START));
  Multiplexer #(.width(5)) multiplexer_4 (
    .in0({5{1'b0}}), .in1(5'b00001), .out(multiplexer_4_out), .sel(comparator_1_gt));
  Register #(.width(5)) MANCHE_COUNT (.D(multiplexer_5_out), .Q(MANCHE_COUNT_q), .clk(clock_1_out));  // open: en, clr
  Adder #(.width(5)) adder_2 (.a(multiplexer_4_out), .b(MANCHE_COUNT_q), .out(adder_2_out));  // open: cin, cout
  Multiplexer #(.width(5)) multiplexer_5 (.in0(adder_2_out), .in1({5{1'b0}}), .out(multiplexer_5_out), .sel(START));
  Register #(.width(5)) ADVANTAGE_REGISTER (
    .D(multiplexer_3_out), .Q(ADVANTAGE_REGISTER_q), .clk(clock_1_out));  // open: en, clr
  Clock clock_1 (.out(clock_1_out));
endmodule
