// Logisim project TESTAMI3.circ as structural Verilog: 1 circuit, main circuit controllaMossaRip2
module controllaMossaRip2 (
  input  [1:0] preManche,
  input  [1:0] in_2,
  input  [1:0] in_3,
  output [1:0] manche
);

  wire clock_1_out, comparator_1_eq;
  wire [1:0] multiplexer_1_out, multiplexer_2_out, multiplexer_3_out, not_1_out, register_1_q, register_2_q;
  wire [3:0] adder_1_out, register_3_q;

  Multiplexer #(.select(2), .width(2)) multiplexer_1 (
    .in0(register_1_q), .in1(manche), .in2(manche), .in3(2'b00), .out(multiplexer_1_out), .sel(manche));
  Register #(.width(2)) register_1 (.D(multiplexer_1_out), .Q(register_1_q), .clk(clock_1_out));  // open: en, clr
  RAM #(.addrWidth(4), .dataWidth(2)) ram_1 (
    .addr(register_3_q), .we(clock_1_out), .clk(clock_1_out), .din(in_2));  // open: oe, dout
  Clock clock_1 (.out(clock_1_out));
  assign not_1_out = ~register_2_q;  // NOT_Gate not_1, 2 bits wide
  Multiplexer #(.select(2), .width(2)) multiplexer_2 (
    .in0(not_1_out), .in1(in_2), .in2(in_3), .in3(not_1_out), .out(multiplexer_2_out), .sel(register_1_q));
  Multiplexer #(.select(2), .width(2)) multiplexer_3 (
    .in0(register_2_q), .in1(in_2), .in2(in_3), .in3(register_2_q), .out(multiplexer_3_out), .sel(manche));
  Register #(.width(2)) register_2 (.D(multiplexer_3_out), .Q(register_2_q), .clk(clock_1_out));  // open: en, clr
  RAM #(.addrWidth(4), .dataWidth(2)) ram_2 (
    .addr(register_3_q), .we(clock_1_out), .clk(clock_1_out), .din(in_3));  // open: oe, dout
  Comparator #(.width(2)) comparator_1 (.a(register_2_q), .b(multiplexer_2_out), .eq(comparator_1_eq));  // open: gt, lt
  Multiplexer #(.width(2)) multiplexer_4 (.in0(preManche), .in1(2'b00), .out(manche), .sel(comparator_1_eq));
  RAM #(.addrWidth(4), .dataWidth(2)) ram_3 (
    .addr(register_3_q), .we(clock_1_out), .clk(clock_1_out), .din(manche));  // open: oe, dout
  Register #(.width(4)) register_3 (.D(adder_1_out), .Q(register_3_q), .clk(clock_1_out));  // open: en, clr
  Adder #(.width(4)) adder_1 (.a(register_3_q), .b(4'b0001), .out(adder_1_out));  // open: cin, cout

  // Notes on the sheet:
  //   gioc che ha vinto prec
  //   1
  //   2
  //   gioc1Move
  //   mossa attuale gioc che ha vinto prec
  //   ultima mossa vinc
  //   gioc2Move
  //   registro mosse e risultato manche
  //   manche
endmodule
