// Logisim project circuitoComb.circ as structural Verilog: 3 circuits, main circuit main
module main (
  input  [1:0] PLAYER1,
  input  [1:0] PLAYER2,
  input  START,
  output [1:0] out_4,
  output [1:0] out_5,
  output [4:0] out_6
);

  wire clock_1_out, undriven;
  wire [1:0] demultiplexer_1_out0, demultiplexer_1_out1, demultiplexer_2_out1;
  wire [4:0] adder_1_out, adder_2_out, multiplexer_3_out, multiplexer_4_out;

  Multiplexer #(.select(2)) multiplexer_1 (.in0(undriven), .sel(demultiplexer_1_out0));  // open: in1, in2, in3, out
  Demultiplexer #(.width(2)) demultiplexer_1 (
    .out0(demultiplexer_1_out0), .out1(demultiplexer_1_out1), .in(PLAYER1), .sel(START));
  Multiplexer #(.select(2)) multiplexer_2 (.sel(demultiplexer_1_out0));  // open: in0, in1, in2, in3, out
  Demultiplexer #(.width(2)) demultiplexer_2 (.out0(out_5), .out1(demultiplexer_2_out1), .in(PLAYER2), .sel(START));
  Multiplexer #(.select(2), .width(5)) multiplexer_3 (
    .in0({5{1'b0}}), .in1(5'b00100), .in2(5'b01000), .in3(5'b01100), .out(multiplexer_3_out),
    .sel(demultiplexer_1_out1));
  Clock clock_1 (.out(clock_1_out));
  Multiplexer #(.select(2), .width(5)) multiplexer_4 (
    .in0({5{1'b0}}), .in1(5'b00001), .in2(5'b00010), .in3(5'b00011), .out(multiplexer_4_out),
    .sel(demultiplexer_2_out1));
  Adder #(.width(5)) adder_1 (.a(multiplexer_4_out), .b(multiplexer_3_out), .out(adder_1_out));  // open: cin, cout
  Adder #(.width(5)) adder_2 (.a(adder_1_out), .b(5'b00100), .out(adder_2_out));  // open: cin, cout
  Register #(.width(5)) MAX_MANCHE (.D(adder_2_out), .Q(out_6), .clk(clock_1_out));  // open: en, clr
endmodule

module circuito_combinatorio (
  input  [1:0] in_1,
  input  [1:0] in_2,
  input  [1:0] in_3,
  input  [1:0] in_4,
  input  in_5,
  input  in_6,
  input  in_7,
  input  in_8,
  input  in_9,
  input  in_10,
  input  in_11,
  input  in_12,
  input  [1:0] in_13,
  input  [1:0] in_14,
  input  [1:0] in_15,
  input  [1:0] in_16,
  input  [1:0] in_17,
  input  [1:0] in_18,
  input  [1:0] in_19,
  input  [1:0] in_20,
  input  [1:0] in_21,
  input  [3:0] in_22,
  input  [3:0] in_23,
  input  [1:0] in_24,
  input  [3:0] in_25,
  input  [3:0] in_26,
  input  [1:0] in_27,
  input  [3:0] in_28,
  input  [3:0] in_29,
  input  [3:0] in_30,
  input  [3:0] in_31,
  input  [1:0] in_32,
  input  [1:0] in_33,
  input  [1:0] in_34,
  input  [1:0] in_35,
  input  in_36,
  input  in_37,
  input  in_38,
  input  in_39,
  input  [1:0] in_40,
  output [1:0] out_41,
  output [1:0] out_42,
  output [1:0] out_43,
  output [3:0] out_44
);

  wire and_1_out, and_2_out, and_3_out, and_4_out, multiplexer_1_out, multiplexer_2_out, multiplexer_5_out,
       multiplexer_7_out, multiplexer_8_out, multiplexer_10_out, multiplexer_11_out, multiplexer_13_out,
       multiplexer_14_out, multiplexer_15_out, multiplexer_17_out, multiplexer_19_out, nand_1_out, not_1_out,
       not_2_out, or_1_out, or_2_out, or_3_out, or_4_out, xor_1_out, xor_2_out;
  wire [1:0] adder_1_out, multiplexer_3_out, multiplexer_4_out, multiplexer_9_out, multiplexer_12_out,
       multiplexer_16_out, multiplexer_18_out;
  wire [3:0] multiplexer_20_out, multiplexer_21_out;

  Multiplexer #(.select(2)) multiplexer_1 (
    .in0(in_11), .in1(in_11), .in2(in_7), .in3(in_7), .out(multiplexer_1_out), .sel(in_3));
  Multiplexer #(.select(2)) multiplexer_2 (
    .in0(in_11), .in1(in_7), .in2(in_11), .in3(in_7), .out(multiplexer_2_out), .sel(in_3));
  xor xor_1 (xor_1_out, multiplexer_1_out, multiplexer_10_out);
  Multiplexer #(.width(2)) multiplexer_3 (.in0(in_13), .in1(in_14), .out(multiplexer_3_out), .sel(xor_1_out));
  Multiplexer #(.select(2), .width(2)) multiplexer_4 (
    .in0(in_16), .in1(adder_1_out), .in2(adder_1_out), .in3(adder_1_out), .out(multiplexer_4_out), .sel(in_3));
  Multiplexer #(.select(2)) multiplexer_5 (
    .in0(in_38), .in1(in_38), .in2(in_36), .in3(in_36), .out(multiplexer_5_out), .sel(in_32));
  LED led_1 (.in(multiplexer_5_out));
  or or_1 (or_1_out, multiplexer_5_out, multiplexer_7_out);
  Multiplexer #(.select(2), .width(2)) multiplexer_6 (
    .in0(in_16), .in1(multiplexer_4_out), .in2(multiplexer_4_out), .in3(multiplexer_4_out), .out(out_42),
    .sel(in_4));
  Multiplexer #(.select(2)) multiplexer_7 (
    .in0(in_38), .in1(in_36), .in2(in_38), .in3(in_36), .out(multiplexer_7_out), .sel(in_32));
  LED led_2 (.in(multiplexer_7_out));
  Multiplexer #(.select(2)) multiplexer_8 (
    .in0(in_12), .in1(in_12), .in2(in_8), .in3(in_8), .out(multiplexer_8_out), .sel(in_4));
  Multiplexer #(.width(2)) multiplexer_9 (.in0(in_14), .in1(in_15), .out(multiplexer_9_out), .sel(xor_2_out));
  Adder #(.width(2)) adder_1 (.a(multiplexer_9_out), .b(multiplexer_3_out), .out(adder_1_out));  // open: cin, cout
  nand nand_1 (nand_1_out, or_1_out, or_2_out);
  Multiplexer #(.select(2)) multiplexer_10 (
    .in0(in_12), .in1(in_8), .in2(in_12), .in3(in_8), .out(multiplexer_10_out), .sel(in_4));
  xor xor_2 (xor_2_out, multiplexer_2_out, multiplexer_8_out);
  Multiplexer #(.select(2)) multiplexer_11 (
    .in0(in_39), .in1(in_39), .in2(in_37), .in3(in_37), .out(multiplexer_11_out), .sel(in_33));
  LED led_3 (.in(multiplexer_11_out));
  Multiplexer #(.width(2)) multiplexer_12 (.in1(in_40), .out(multiplexer_12_out), .sel(nand_1_out));  // open: in0
  Multiplexer #(.select(2)) multiplexer_13 (
    .in0(in_39), .in1(in_37), .in2(in_39), .in3(in_37), .out(multiplexer_13_out), .sel(in_33));
  LED led_4 (.in(multiplexer_13_out));
  or or_2 (or_2_out, multiplexer_11_out, multiplexer_13_out);
  Multiplexer #(.select(2)) multiplexer_14 (
    .in0(in_9), .in1(in_9), .in2(in_5), .in3(in_5), .out(multiplexer_14_out), .sel(in_1));
  and and_1 (and_1_out, multiplexer_14_out, multiplexer_17_out);
  Multiplexer #(.select(2)) multiplexer_15 (
    .in0(in_9), .in1(in_5), .in2(in_9), .in3(in_5), .out(multiplexer_15_out), .sel(in_1));
  and and_2 (and_2_out, multiplexer_15_out, multiplexer_19_out);
  or or_3 (or_3_out, and_1_out, and_2_out);
  Multiplexer #(.width(2)) multiplexer_16 (.in0(in_17), .in1(in_18), .out(multiplexer_16_out), .sel(or_3_out));
  Multiplexer #(.select(2)) multiplexer_17 (
    .in0(in_10), .in1(in_10), .in2(in_6), .in3(in_6), .out(multiplexer_17_out), .sel(in_2));
  not not_1 (not_1_out, multiplexer_17_out);
  and and_3 (and_3_out, multiplexer_14_out, not_1_out);
  Multiplexer #(.width(2)) multiplexer_18 (.in0(in_19), .in1(in_18), .out(multiplexer_18_out), .sel(or_4_out));
  Adder #(.width(2)) adder_2 (.a(multiplexer_18_out), .b(multiplexer_16_out), .out(out_41));  // open: cin, cout
  Multiplexer #(.select(2)) multiplexer_19 (
    .in0(in_10), .in1(in_6), .in2(in_10), .in3(in_6), .out(multiplexer_19_out), .sel(in_2));
  not not_2 (not_2_out, multiplexer_14_out);
  and and_4 (and_4_out, not_2_out, multiplexer_17_out);
  or or_4 (or_4_out, and_3_out, and_4_out);
  Multiplexer #(.select(2), .width(4)) multiplexer_20 (
    .in0(in_30), .in1(in_28), .in2(in_25), .in3(in_22), .out(multiplexer_20_out), .sel(in_34));
  Multiplexer #(.select(2), .width(4)) multiplexer_21 (
    .in0(in_31), .in1(in_29), .in2(in_26), .in3(in_23), .out(multiplexer_21_out), .sel(in_35));
  Adder #(.width(4)) adder_3 (.a(multiplexer_21_out), .b(multiplexer_20_out), .out(out_44));  // open: cin, cout
  Multiplexer #(.select(4), .width(2)) multiplexer_22 (
    .in0(in_27), .in1(in_27), .in2(in_27), .in3(in_27), .in4(in_27), .in5(in_20), .in6(in_21), .in7(in_24),
    .in8(in_27), .in9(in_24), .in10(in_20), .in11(in_21), .in12(in_27), .in13(in_21), .in14(in_24),
    .in15(in_20), .out(out_43), .sel(out_44));

  // Notes on the sheet:
  //   algebra booleana per cui input1 = 00 OR input2 = 00
  //   logica combinatoria personalizzata
endmodule

module circuito_comb (
  input  [1:0] in_1,
  input  [1:0] in_2,
  input  [3:0] in_3,
  input  [3:0] in_4,
  input  [1:0] in_5,
  input  [3:0] in_6,
  input  [3:0] in_7,
  input  [1:0] in_8,
  input  [3:0] in_9,
  input  [3:0] in_10,
  input  [3:0] in_11,
  input  [3:0] in_12,
  input  [1:0] in_13,
  input  [1:0] in_14,
  output [1:0] out_15,
  output [3:0] out_16
);

  wire [3:0] multiplexer_1_out, multiplexer_2_out;

  Multiplexer #(.select(2), .width(4)) multiplexer_1 (
    .in0(in_11), .in1(in_9), .in2(in_6), .in3(in_3), .out(multiplexer_1_out), .sel(in_13));
  Multiplexer #(.select(2), .width(4)) multiplexer_2 (
    .in0(in_12), .in1(in_10), .in2(in_7), .in3(in_4), .out(multiplexer_2_out), .sel(in_14));
  Adder #(.width(4)) adder_1 (.a(multiplexer_2_out), .b(multiplexer_1_out), .out(out_16));  // open: cin, cout
  Multiplexer #(.select(4), .width(2)) multiplexer_3 (
    .in0(in_8), .in1(in_8), .in2(in_8), .in3(in_8), .in4(in_8), .in5(in_1), .in6(in_2), .in7(in_5),
    .in8(in_8), .in9(in_5), .in10(in_1), .in11(in_2), .in12(in_8), .in13(in_2), .in14(in_5), .in15(in_1),
    .out(out_15), .sel(out_16));

  // Notes on the sheet:
  //   logica combinatoria personalizzata
endmodule
