// Logisim project datapath.circ as structural Verilog: 1 circuit, main circuit main
module main (
  input  [1:0] PLAYER1,
  input  [1:0] PLAYER2,
  input  START,
  output [2:0] ADV,
  output [4:0] PLAYED,
  output [4:0] TOTAL
);

  wire and_1_out, and_2_out, and_3_out, and_4_out, clock_1_out, comparator_1_eq, comparator_2_eq,
       comparator_3_eq, comparator_4_eq, comparator_5_eq, comparator_6_eq, comparator_7_eq, comparator_8_eq,
       comparator_9_gt, comparator_10_eq, comparator_11_eq, comparator_12_eq, not_1_out, or_1_out, or_2_out,
       or_3_out;
  wire [1:0] demultiplexer_1_out0, demultiplexer_1_out1, demultiplexer_2_out0, demultiplexer_2_out1,
       multiplexer_4_out, multiplexer_6_out, multiplexer_7_out;
  wire [2:0] adder_1_out, multiplexer_1_out, multiplexer_2_out, multiplexer_3_out, subtractor_1_out;
  wire [4:0] adder_2_out, adder_3_out, adder_4_out, multiplexer_5_out, multiplexer_8_out, multiplexer_9_out,
       multiplexer_10_out, multiplexer_11_out;

  Demultiplexer #(.width(2)) demultiplexer_1 (
    .out0(demultiplexer_1_out0), .out1(demultiplexer_1_out1), .in(PLAYER1), .sel(START));
  Comparator #(.mode("unsigned"), .width(2)) comparator_1 (
    .a(demultiplexer_1_out0), .b(2'b01), .eq(comparator_1_eq));  // open: gt, lt
  Comparator #(.mode("unsigned"), .width(2)) comparator_2 (
    .a(multiplexer_7_out), .b(2'b00), .eq(comparator_2_eq));  // open: gt, lt
  Comparator #(.mode("unsigned"), .width(2)) comparator_3 (
    .a(multiplexer_7_out), .b(2'b11), .eq(comparator_3_eq));  // open: gt, lt
  Comparator #(.mode("unsigned"), .width(2)) comparator_4 (
    .a(demultiplexer_2_out0), .b(2'b11), .eq(comparator_4_eq));  // open: gt, lt
  and and_1 (and_1_out, comparator_1_eq, comparator_4_eq);
  or or_1 (or_1_out, comparator_2_eq, comparator_3_eq);
  Adder #(.width(3)) adder_1 (.a(ADV), .b(multiplexer_3_out), .out(adder_1_out));  // open: cin, cout
  Subtractor #(.width(3)) subtractor_1 (.a(ADV), .b(multiplexer_3_out), .out(subtractor_1_out));  // open: bin, bout
  Demultiplexer #(.width(2)) demultiplexer_2 (
    .out0(demultiplexer_2_out0), .out1(demultiplexer_2_out1), .in(PLAYER2), .sel(START));
  Multiplexer #(.select(2), .width(3)) multiplexer_1 (
    .in0(ADV), .in1(subtractor_1_out), .in2(adder_1_out), .in3(ADV), .out(multiplexer_1_out),
    .sel(multiplexer_7_out));
  Multiplexer #(.width(3)) multiplexer_2 (.in0(multiplexer_1_out), .in1(3'b010), .out(multiplexer_2_out), .sel(START));
  Comparator #(.mode("unsigned"), .width(2)) comparator_5 (
    .a(demultiplexer_1_out0), .b(2'b10), .eq(comparator_5_eq));  // open: gt, lt
  Multiplexer #(.width(3)) multiplexer_3 (.in0(3'b001), .in1(3'b000), .out(multiplexer_3_out), .sel(or_1_out));
  Comparator #(.mode("unsigned"), .width(2)) comparator_6 (
    .a(demultiplexer_2_out0), .b(2'b01), .eq(comparator_6_eq));  // open: gt, lt
  and and_2 (and_2_out, comparator_5_eq, comparator_6_eq);
  or or_2 (or_2_out, and_1_out, and_2_out, and_3_out);
  Multiplexer #(.width(2)) multiplexer_4 (.in0(2'b10), .in1(2'b01), .out(multiplexer_4_out), .sel(or_2_out));
  Register #(.width(3)) GAME_ADV_REGISTER (.D(multiplexer_2_out), .Q(ADV), .clk(clock_1_out));  // open: en, clr
  Multiplexer #(.select(2), .width(5)) multiplexer_5 (
    .in0({5{1'b0}}), .in1(5'b00100), .in2(5'b01000), .in3(5'b01100), .out(multiplexer_5_out),
    .sel(demultiplexer_1_out1));
  Multiplexer #(.width(2)) multiplexer_6 (
    .in0(multiplexer_4_out), .in1(2'b00), .out(multiplexer_6_out), .sel(or_3_out));
  Clock clock_1 (.out(clock_1_out));
  Comparator #(.mode("unsigned"), .width(2)) comparator_7 (
    .a(demultiplexer_1_out0), .b(2'b11), .eq(comparator_7_eq));  // open: gt, lt
  Multiplexer #(.width(2)) multiplexer_7 (
    .in0(multiplexer_6_out), .in1(2'b11), .out(multiplexer_7_out), .sel(and_4_out));
  Multiplexer #(.select(2), .width(5)) multiplexer_8 (
    .in0({5{1'b0}}), .in1(5'b00001), .in2(5'b00010), .in3(5'b00011), .out(multiplexer_8_out),
    .sel(demultiplexer_2_out1));
  Adder #(.width(5)) adder_2 (.a(multiplexer_8_out), .b(multiplexer_5_out), .out(adder_2_out));  // open: cin, cout
  Comparator #(.mode("unsigned"), .width(2)) comparator_8 (
    .a(demultiplexer_2_out0), .b(2'b10), .eq(comparator_8_eq));  // open: gt, lt
  and and_3 (and_3_out, comparator_7_eq, comparator_8_eq);
  Comparator #(.mode("unsigned"), .width(2)) comparator_9 (
    .a(multiplexer_7_out), .b(2'b00), .gt(comparator_9_gt));  // open: eq, lt
  Adder #(.width(5)) adder_3 (.a(adder_2_out), .b(5'b00100), .out(adder_3_out));  // open: cin, cout
  Multiplexer #(.width(5)) multiplexer_9 (
    .in0({5{1'b0}}), .in1(5'b00001), .out(multiplexer_9_out), .sel(comparator_9_gt));
  Multiplexer #(.width(5)) multiplexer_10 (.in0(TOTAL), .in1(adder_3_out), .out(multiplexer_10_out), .sel(START));
  Comparator #(.mode("unsigned"), .width(2)) comparator_10 (
    .a(demultiplexer_1_out0), .b(2'b00), .eq(comparator_10_eq));  // open: gt, lt
  Adder #(.width(5)) adder_4 (.a(multiplexer_9_out), .b(PLAYED), .out(adder_4_out));  // open: cin, cout
  Comparator #(.mode("unsigned"), .width(2)) comparator_11 (
    .a(demultiplexer_2_out0), .b(2'b00), .eq(comparator_11_eq));  // open: gt, lt
  or or_3 (or_3_out, comparator_10_eq, comparator_11_eq);
  Multiplexer #(.width(5)) multiplexer_11 (.in0(adder_4_out), .in1({5{1'b0}}), .out(multiplexer_11_out), .sel(START));
  Register #(.width(5)) TOTAL_MANCHE_REGISTER (.D(multiplexer_10_out), .Q(TOTAL), .clk(clock_1_out));  // open: en, clr
  not not_1 (not_1_out, or_3_out);
  and and_4 (and_4_out, not_1_out, comparator_12_eq);
  Comparator #(.mode("unsigned"), .width(2)) comparator_12 (
    .a(demultiplexer_2_out0), .b(demultiplexer_1_out0), .eq(comparator_12_eq));  // open: gt, lt
  Register #(.width(5)) PLAYED_MANCHE_REGISTER (
    .D(multiplexer_11_out), .Q(PLAYED), .clk(clock_1_out));  // open: en, clr
endmodule
