// Logisim project last_move_check_test.circ as structural Verilog: 2 circuits, main circuit main
module main (
  input  [1:0] P1_MOVE,
  input  [1:0] P2_MOVE,
  input  START,
  output [4:0] TOTAL,
  output [1:0] WINNING_PLAYER,
  output [4:0] PLD,
  output ENDABLE,
  output W1,
  output W2,
  output D
);

  wire adder_3_cout, and_1_out, and_2_out, and_3_out, and_4_out, and_5_out, CLK_out, comparator_1_eq,
       comparator_2_eq, comparator_3_eq, comparator_4_eq, comparator_5_eq, comparator_6_eq, comparator_7_eq,
       comparator_8_eq, comparator_9_eq, comparator_10_eq, comparator_11_eq, comparator_12_eq,
       comparator_13_eq, comparator_14_eq, comparator_15_gt, comparator_16_eq, comparator_17_gt,
       comparator_18_eq, comparator_19_gt, multiplexer_8_out, multiplexer_10_out, multiplexer_11_out,
       nor_1_out, nor_2_out, not_2_out, or_1_out, or_2_out, or_3_out, WIN1_out, WIN2_out;
  wire [1:0] multiplexer_1_out, multiplexer_2_out, multiplexer_3_out, multiplexer_5_out, multiplexer_6_out,
       multiplexer_7_out, not_1_out, register_1_q, register_2_q;
  wire [4:0] adder_1_out, adder_2_out, adder_3_out, adder_4_out, adder_5_out, COUNT_1_q, COUNT_2_q,
       multiplexer_12_out, multiplexer_13_out, multiplexer_14_out, multiplexer_15_out, multiplexer_16_out,
       multiplexer_17_out, multiplexer_18_out, multiplexer_19_out, multiplexer_20_out, multiplexer_21_out,
       subtractor_1_out, subtractor_2_out;

  Comparator #(.mode("unsigned"), .width(2)) comparator_1 (
    .a(P1_MOVE), .b(2'b01), .eq(comparator_1_eq));  // open: gt, lt
  Multiplexer #(.select(2), .width(2)) multiplexer_1 (
    .in0(register_2_q), .in1(multiplexer_7_out), .in2(multiplexer_7_out), .in3(2'b00),
    .out(multiplexer_1_out), .sel(multiplexer_7_out));
  Comparator #(.mode("unsigned"), .width(2)) comparator_2 (
    .a(P2_MOVE), .b(2'b11), .eq(comparator_2_eq));  // open: gt, lt
  and and_1 (and_1_out, comparator_1_eq, comparator_2_eq);
  Comparator #(.mode("unsigned"), .width(2)) comparator_3 (
    .a(WINNING_PLAYER), .b(2'b01), .eq(comparator_3_eq));  // open: gt, lt
  Comparator #(.mode("unsigned"), .width(2)) comparator_4 (
    .a(WINNING_PLAYER), .b(2'b11), .eq(comparator_4_eq));  // open: gt, lt
  Comparator #(.mode("unsigned"), .width(2)) comparator_5 (
    .a(WINNING_PLAYER), .b(2'b00), .eq(comparator_5_eq));  // open: gt, lt
  Comparator #(.mode("unsigned"), .width(2)) comparator_6 (
    .a(WINNING_PLAYER), .b(2'b10), .eq(comparator_6_eq));  // open: gt, lt
  nor nor_1 (nor_1_out, comparator_4_eq, comparator_5_eq);
  Multiplexer #(.select(2), .width(2)) multiplexer_2 (
    .in0(register_1_q), .in1(P1_MOVE), .in2(P2_MOVE), .in3(2'b00), .out(multiplexer_2_out),
    .sel(multiplexer_7_out));
  Register #(.width(2)) register_1 (.D(multiplexer_2_out), .Q(register_1_q), .clk(CLK_out));  // open: en, clr
  Multiplexer #(.select(2), .width(2)) multiplexer_3 (
    .in0(not_1_out), .in1(P1_MOVE), .in2(P2_MOVE), .in3(not_1_out), .out(multiplexer_3_out),
    .sel(register_2_q));
  Register #(.width(2)) register_2 (.D(multiplexer_1_out), .Q(register_2_q));  // open: en, clk, clr
  Comparator #(.mode("unsigned"), .width(2)) comparator_7 (
    .a(P1_MOVE), .b(2'b10), .eq(comparator_7_eq));  // open: gt, lt
  Multiplexer #(.width(2)) multiplexer_4 (
    .in0(multiplexer_7_out), .in1(2'b00), .out(WINNING_PLAYER), .sel(comparator_11_eq));
  assign not_1_out = ~register_1_q;  // NOT_Gate not_1, 2 bits wide
  Comparator #(.mode("unsigned"), .width(2)) comparator_8 (
    .a(P2_MOVE), .b(2'b01), .eq(comparator_8_eq));  // open: gt, lt
  and and_2 (and_2_out, comparator_7_eq, comparator_8_eq);
  or or_1 (or_1_out, and_1_out, and_2_out, and_3_out);
  Multiplexer #(.width(2)) multiplexer_5 (.in0(2'b10), .in1(2'b01), .out(multiplexer_5_out), .sel(or_1_out));
  Multiplexer #(.width(2)) multiplexer_6 (
    .in0(multiplexer_5_out), .in1(2'b00), .out(multiplexer_6_out), .sel(or_2_out));
  and WIN1 (WIN1_out, comparator_3_eq, nor_1_out);
  and WIN2 (WIN2_out, nor_1_out, comparator_6_eq);
  Comparator #(.mode("unsigned"), .width(2)) comparator_9 (
    .a(P1_MOVE), .b(2'b11), .eq(comparator_9_eq));  // open: gt, lt
  Multiplexer #(.width(2)) multiplexer_7 (
    .in0(multiplexer_6_out), .in1(2'b11), .out(multiplexer_7_out), .sel(and_4_out));
  Multiplexer multiplexer_8 (.in0(WIN1_out), .in1(1'b0), .out(multiplexer_8_out), .sel(START));
  Multiplexer multiplexer_9 (.in0(comparator_4_eq), .in1(1'b0), .sel(START));  // open: out
  Multiplexer multiplexer_10 (.in0(comparator_5_eq), .in1(1'b0), .out(multiplexer_10_out), .sel(START));
  Multiplexer multiplexer_11 (.in0(WIN2_out), .in1(1'b0), .out(multiplexer_11_out), .sel(START));
  Comparator #(.mode("unsigned"), .width(2)) comparator_10 (
    .a(P2_MOVE), .b(2'b10), .eq(comparator_10_eq));  // open: gt, lt
  and and_3 (and_3_out, comparator_9_eq, comparator_10_eq);
  Comparator #(.mode("unsigned"), .width(2)) comparator_11 (
    .a(register_1_q), .b(multiplexer_3_out), .eq(comparator_11_eq));  // open: gt, lt
  Comparator #(.mode("unsigned"), .width(2)) comparator_12 (
    .a(P1_MOVE), .b(2'b00), .eq(comparator_12_eq));  // open: gt, lt
  Comparator #(.mode("unsigned"), .width(2)) comparator_13 (
    .a(P2_MOVE), .b(2'b00), .eq(comparator_13_eq));  // open: gt, lt
  or or_2 (or_2_out, comparator_12_eq, comparator_13_eq);
  not not_2 (not_2_out, or_2_out);
  and and_4 (and_4_out, not_2_out, comparator_14_eq);
  Adder #(.width(5)) adder_1 (.a(PLD), .b(5'b00001), .out(adder_1_out));  // open: cin, cout
  Multiplexer #(.width(5)) multiplexer_12 (
    .in0(adder_1_out), .in1(PLD), .out(multiplexer_12_out), .sel(multiplexer_10_out));
  Multiplexer #(.width(5)) multiplexer_13 (
    .in0(multiplexer_12_out), .in1({5{1'b0}}), .out(multiplexer_13_out), .sel(START));
  Clock CLK (.out(CLK_out));
  Comparator #(.mode("unsigned"), .width(2)) comparator_14 (
    .a(P2_MOVE), .b(P1_MOVE), .eq(comparator_14_eq));  // open: gt, lt
  Register #(.width(5)) PLAYED (.D(multiplexer_13_out), .Q(PLD), .clk(CLK_out));  // open: en, clr
  Multiplexer #(.width(5)) multiplexer_14 (
    .in0(COUNT_1_q), .in1(adder_2_out), .out(multiplexer_14_out), .sel(multiplexer_8_out));
  Multiplexer #(.width(5)) multiplexer_15 (
    .in0(multiplexer_14_out), .in1({5{1'b0}}), .out(multiplexer_15_out), .sel(START));
  Multiplexer #(.select(2), .width(5)) multiplexer_16 (
    .in0({5{1'b0}}), .in1(5'b00100), .in2(5'b01000), .in3(5'b01100), .out(multiplexer_16_out), .sel(P1_MOVE));
  Adder #(.width(5)) adder_2 (.a(COUNT_1_q), .b(5'b00001), .out(adder_2_out));  // open: cin, cout
  Register #(.width(5)) COUNT_1 (.D(multiplexer_15_out), .Q(COUNT_1_q), .clk(CLK_out));  // open: en, clr
  Multiplexer #(.select(2), .width(5)) multiplexer_17 (
    .in0({5{1'b0}}), .in1(5'b00001), .in2(5'b00010), .in3(5'b00011), .out(multiplexer_17_out), .sel(P2_MOVE));
  Adder #(.width(5)) adder_3 (
    .a(multiplexer_17_out), .b(multiplexer_16_out), .out(adder_3_out), .cout(adder_3_cout));  // open: cin
  Adder #(.width(5)) adder_4 (.a(adder_3_out), .b(5'b00100), .out(adder_4_out));  // open: cin, cout
  Multiplexer #(.width(5)) multiplexer_18 (
    .in0(COUNT_2_q), .in1(adder_5_out), .out(multiplexer_18_out), .sel(multiplexer_11_out));
  Multiplexer #(.width(5)) multiplexer_19 (
    .in0(multiplexer_18_out), .in1({5{1'b0}}), .out(multiplexer_19_out), .sel(START));
  Multiplexer #(.width(5)) multiplexer_20 (.in0(TOTAL), .in1(adder_4_out), .out(multiplexer_20_out), .sel(START));
  Adder #(.width(5)) adder_5 (.a(COUNT_2_q), .b(5'b00001), .out(adder_5_out));  // open: cin, cout
  Register #(.width(5)) COUNT_2 (.D(multiplexer_19_out), .Q(COUNT_2_q), .clk(CLK_out));  // open: en, clr
  Comparator #(.width(5)) comparator_15 (.a(PLD), .b(5'b00011), .gt(comparator_15_gt));  // open: eq, lt
  Comparator #(.width(5)) comparator_16 (.a(TOTAL), .b(PLD), .eq(comparator_16_eq));  // open: gt, lt
  Register #(.width(5)) FINAL (.D(multiplexer_20_out), .Q(TOTAL), .clk(CLK_out));  // open: en, clr
  or or_3 (or_3_out, comparator_15_gt, comparator_16_eq);
  Comparator #(.mode("unsigned"), .width(5)) comparator_17 (
    .a(COUNT_1_q), .b(COUNT_2_q), .gt(comparator_17_gt));  // open: eq, lt
  Comparator #(.mode("unsigned"), .width(5)) comparator_18 (
    .a(COUNT_2_q), .b(COUNT_1_q), .eq(comparator_18_eq));  // open: gt, lt
  Comparator #(.width(5)) comparator_19 (.a(multiplexer_21_out), .b(5'b00001), .gt(comparator_19_gt));  // open: eq, lt
  nor nor_2 (nor_2_out, comparator_17_gt, comparator_18_eq);
  Subtractor #(.width(5)) subtractor_1 (.a(COUNT_1_q), .b(COUNT_2_q), .out(subtractor_1_out));  // open: bin, bout
  Subtractor #(.width(5)) subtractor_2 (.a(COUNT_2_q), .b(COUNT_1_q), .out(subtractor_2_out));  // open: bin, bout
  Multiplexer #(.width(5)) multiplexer_21 (
    .in0(subtractor_2_out), .in1(subtractor_1_out), .out(multiplexer_21_out), .sel(comparator_17_gt));
  and and_5 (and_5_out, comparator_19_gt, comparator_15_gt);
  or or_4 (ENDABLE, and_5_out, comparator_16_eq);
  and and_6 (W1, comparator_17_gt, or_3_out);
  and and_7 (W2, nor_2_out, or_3_out);
  and and_8 (D, or_3_out, comparator_18_eq);

  // Notes on the sheet:
  //   p1move
  //   p2move
  //   MANCHE WINNER LOGIC
  //   gioc1move
  //   gioc2move
  //   I: winning player
  //   CONTROL SIGNALS
  //   ultima mossa che ha vinto
  //   draw
  //   invalid
  //   mossa attuale del gioc che ha vin ult. man.
  //   giocatore che effettivamente ha vinto nella manche precedente
  //   O: winning player
  //   SELECT: invalid
  //   SELECT: start signal
  //   se 1 manche non valida
  //   perchè mossa vincente
  //   è stata ripetuta
  //   GAME COUNT
  //   SET TOTAL MANCHE
  //   ADVANTAGE CALCULATOR
  //   END GAME
  //   O: vantaggio
  //   O (da sx): draw, w2, w1
  //   O: w1
  //   O: w2
  //   O: d
  //   O: endable
  //   NOTE:
  //   1 manca il controllo sulla mossa precedente
  //   2 la logica winning manche sara' riassunta con una logica combinatoria personalizzata
  //   3 la logica total manche sara' riassunta con una logica combinatoria personalizzata
endmodule

module controlloMossaRipetuta (
  input  [1:0] gioc1move,
  input  [1:0] gioc2move,
  output [1:0] out_3,
  output [1:0] out_4
);

  wire and_1_out, and_2_out, and_3_out, and_4_out, clock_1_out, comparator_1_eq, comparator_2_eq,
       comparator_3_eq, comparator_4_eq, comparator_5_eq, comparator_6_eq, comparator_7_eq, comparator_8_eq,
       comparator_9_eq, comparator_10_eq, not_2_out, or_1_out, or_2_out;
  wire [1:0] multiplexer_1_out, multiplexer_2_out, multiplexer_3_out, multiplexer_4_out, multiplexer_6_out,
       not_1_out, register_1_q, register_2_q;

  Multiplexer #(.select(2), .width(2)) multiplexer_1 (
    .in0(register_2_q), .in1(out_3), .in2(out_3), .in3(2'b00), .out(multiplexer_1_out), .sel(out_3));
  Comparator #(.mode("unsigned"), .width(2)) comparator_1 (
    .a(gioc1move), .b(2'b01), .eq(comparator_1_eq));  // open: gt, lt
  and and_1 (and_1_out, comparator_1_eq, comparator_2_eq);
  Comparator #(.mode("unsigned"), .width(2)) comparator_2 (
    .a(gioc2move), .b(2'b11), .eq(comparator_2_eq));  // open: gt, lt
  Multiplexer #(.select(2), .width(2)) multiplexer_2 (
    .in0(register_1_q), .in1(gioc1move), .in2(gioc2move), .in3(2'b00), .out(multiplexer_2_out), .sel(out_3));
  Register #(.width(2)) register_1 (.D(multiplexer_2_out), .Q(register_1_q), .clk(clock_1_out));  // open: en, clr
  Multiplexer #(.select(2), .width(2)) multiplexer_3 (
    .in0(not_1_out), .in1(gioc1move), .in2(gioc2move), .in3(not_1_out), .out(multiplexer_3_out),
    .sel(register_2_q));
  Register #(.width(2)) register_2 (.D(multiplexer_1_out), .Q(register_2_q), .clk(clock_1_out));  // open: en, clr
  assign not_1_out = ~register_1_q;  // NOT_Gate not_1, 2 bits wide
  Comparator #(.mode("unsigned"), .width(2)) comparator_3 (
    .a(gioc1move), .b(2'b10), .eq(comparator_3_eq));  // open: gt, lt
  and and_2 (and_2_out, comparator_3_eq, comparator_4_eq);
  or or_1 (or_1_out, and_1_out, and_2_out, and_3_out);
  Comparator #(.mode("unsigned"), .width(2)) comparator_4 (
    .a(gioc2move), .b(2'b01), .eq(comparator_4_eq));  // open: gt, lt
  Multiplexer #(.width(2)) multiplexer_4 (.in0(2'b10), .in1(2'b01), .out(multiplexer_4_out), .sel(or_1_out));
  Multiplexer #(.width(2)) multiplexer_5 (.in0(out_3), .in1(2'b00), .out(out_4), .sel(comparator_6_eq));
  Multiplexer #(.width(2)) multiplexer_6 (
    .in0(multiplexer_4_out), .in1(2'b00), .out(multiplexer_6_out), .sel(or_2_out));
  Multiplexer #(.width(2)) multiplexer_7 (.in0(multiplexer_6_out), .in1(2'b11), .out(out_3), .sel(and_4_out));
  Comparator #(.mode("unsigned"), .width(2)) comparator_5 (
    .a(gioc1move), .b(2'b11), .eq(comparator_5_eq));  // open: gt, lt
  and and_3 (and_3_out, comparator_5_eq, comparator_7_eq);
  Clock clock_1 (.out(clock_1_out));
  Comparator #(.mode("unsigned"), .width(2)) comparator_6 (
    .a(register_1_q), .b(multiplexer_3_out), .eq(comparator_6_eq));  // open: gt, lt
  Comparator #(.mode("unsigned"), .width(2)) comparator_7 (
    .a(gioc2move), .b(2'b10), .eq(comparator_7_eq));  // open: gt, lt
  Comparator #(.mode("unsigned"), .width(2)) comparator_8 (
    .a(gioc1move), .b(2'b00), .eq(comparator_8_eq));  // open: gt, lt
  or or_2 (or_2_out, comparator_8_eq, comparator_9_eq);
  Comparator #(.mode("unsigned"), .width(2)) comparator_9 (
    .a(gioc2move), .b(2'b00), .eq(comparator_9_eq));  // open: gt, lt
  not not_2 (not_2_out, or_2_out);
  and and_4 (and_4_out, not_2_out, comparator_10_eq);
  Comparator #(.mode("unsigned"), .width(2)) comparator_10 (
    .a(gioc2move), .b(gioc1move), .eq(comparator_10_eq));  // open: gt, lt

  // Notes on the sheet:
  //   p1move
  //   p2move
  //   gioc1move
  //   gioc2move
  //   2
  //   ultima mossa che ha vinto
  //   manche
  //   mossa attuale del gioc che ha vin ult. man.
  //   giocatore che effettivamente ha vinto nella manche precedente
  //   1
  //   valore manche dopo il controllo
  //   se 1 manche non valida
  //   perchè mossa vincente
  //   è stata ripetuta
endmodule
