// Logisim project new_datapath.circ as structural Verilog: 7 circuits, main circuit main
module main (
  input  [1:0] P1,
  input  [1:0] P2,
  input  START,
  output [4:0] TO_PLAY,
  output [4:0] PLAYED,
  output [4:0] ADV,
  output STOP,
  output G1,
  output G2,
  output GD
);

  wire CLK_out, game_adv_1_adv1, game_adv_1_adv2, game_adv_1_draw, match_winner_2_1_invalid,
       match_winner_2_1_win1, match_winner_2_1_win2;

  match_winner_2 match_winner_2_1 (
    .P1(P1), .P2(P2), .START(START), .CLK(CLK_out), .WIN1(match_winner_2_1_win1),
    .WIN2(match_winner_2_1_win2), .INVALID(match_winner_2_1_invalid));
  Clock CLK (.out(CLK_out));
  set_total_manche set_total_manche_1 (.CLK(CLK_out), .START(START), .P1(P1), .P2(P2), .TO_PLAY(TO_PLAY));
  game_adv game_adv_1 (
    .CLK(CLK_out), .INVALID(match_winner_2_1_invalid), .WIN1(match_winner_2_1_win1),
    .WIN2(match_winner_2_1_win2), .START(START), .ADV1(game_adv_1_adv1), .ADV2(game_adv_1_adv2),
    .DRAW(game_adv_1_draw), .ADV(ADV));
  game_count game_count_1 (.CLK(CLK_out), .START(START), .INVALID(match_winner_2_1_invalid), .PLAYED(PLAYED));
  end_game end_game_1 (
    .MATCH_ADV(ADV), .DRAW(game_adv_1_draw), .ADV1(game_adv_1_adv2), .ADV2(game_adv_1_adv1), .PLAYED(PLAYED),
    .TO_PLAY(TO_PLAY), .GAME1(G1), .GAME2(G2), .GAMED(GD), .STOP(STOP));
endmodule

module match_winner (
  input  [1:0] P1,
  input  [1:0] P2,
  input  START,
  input  CLK,
  output WIN1,
  output WIN2,
  output INVALID
);

  wire and_1_out, and_2_out, and_3_out, and_4_out, comparator_1_eq, comparator_2_eq, comparator_3_eq,
       comparator_4_eq, comparator_5_eq, comparator_6_eq, comparator_7_eq, comparator_8_eq, comparator_9_eq,
       comparator_10_eq, comparator_11_eq, comparator_12_eq, comparator_13_eq, comparator_14_eq, nor_1_out,
       not_1_out, or_1_out, or_2_out, or_3_out, W1_out, W2_out;
  wire [1:0] LAST_P1_q, LAST_P2_q, LAST_WINNER_q, multiplexer_1_out, multiplexer_2_out, multiplexer_3_out,
       multiplexer_4_out, multiplexer_5_out, multiplexer_6_out, multiplexer_7_out;

  Comparator #(.mode("unsigned"), .width(2)) comparator_1 (.a(P1), .b(2'b01), .eq(comparator_1_eq));  // open: gt, lt
  Register #(.width(2)) LAST_P1 (.D(P1), .Q(LAST_P1_q), .clk(CLK));  // open: en, clr
  Comparator #(.mode("unsigned"), .width(2)) comparator_2 (.a(P2), .b(2'b11), .eq(comparator_2_eq));  // open: gt, lt
  and and_1 (and_1_out, comparator_1_eq, comparator_2_eq);
  Register #(.width(2)) LAST_P2 (.D(P2), .Q(LAST_P2_q), .clk(CLK));  // open: en, clr
  Multiplexer #(.select(2), .width(2)) multiplexer_1 (
    .in0(2'b00), .in1(LAST_P1_q), .in2(LAST_P2_q), .in3(2'b00), .out(multiplexer_1_out), .sel(LAST_WINNER_q));
  Multiplexer #(.width(2)) multiplexer_2 (.in0(multiplexer_1_out), .in1(2'b00), .out(multiplexer_2_out), .sel(START));
  Comparator #(.mode("unsigned"), .width(2)) comparator_3 (
    .a(multiplexer_7_out), .b(2'b01), .eq(comparator_3_eq));  // open: gt, lt
  Comparator #(.mode("unsigned"), .width(2)) comparator_4 (
    .a(multiplexer_7_out), .b(2'b10), .eq(comparator_4_eq));  // open: gt, lt
  Comparator #(.mode("unsigned"), .width(2)) comparator_5 (
    .a(multiplexer_7_out), .b(2'b11), .eq(comparator_5_eq));  // open: gt, lt
  Comparator #(.mode("unsigned"), .width(2)) comparator_6 (
    .a(multiplexer_7_out), .b(2'b00), .eq(comparator_6_eq));  // open: gt, lt
  Register #(.width(2)) LAST_WINNER (.D(multiplexer_7_out), .Q(LAST_WINNER_q), .clk(CLK));  // open: en, clr
  Comparator #(.mode("unsigned"), .width(2)) comparator_7 (.a(P1), .b(2'b10), .eq(comparator_7_eq));  // open: gt, lt
  Comparator #(.mode("unsigned"), .width(2)) comparator_8 (.a(P2), .b(2'b01), .eq(comparator_8_eq));  // open: gt, lt
  and and_2 (and_2_out, comparator_7_eq, comparator_8_eq);
  or or_1 (or_1_out, and_1_out, and_2_out, and_3_out);
  Multiplexer #(.width(2)) multiplexer_3 (.in0(2'b10), .in1(2'b01), .out(multiplexer_3_out), .sel(or_1_out));
  nor nor_1 (nor_1_out, comparator_5_eq, comparator_6_eq);
  Multiplexer #(.select(2), .width(2)) multiplexer_4 (
    .in0(2'b11), .in1(P1), .in2(P2), .in3(2'b11), .out(multiplexer_4_out), .sel(LAST_WINNER_q));
  Multiplexer #(.width(2)) multiplexer_5 (.in0(multiplexer_4_out), .in1(2'b00), .out(multiplexer_5_out), .sel(START));
  Multiplexer #(.width(2)) multiplexer_6 (
    .in0(multiplexer_3_out), .in1(2'b00), .out(multiplexer_6_out), .sel(or_2_out));
  Comparator #(.mode("unsigned"), .width(2)) comparator_9 (
    .a(multiplexer_5_out), .b(multiplexer_2_out), .eq(comparator_9_eq));  // open: gt, lt
  Comparator #(.mode("unsigned"), .width(2)) comparator_10 (.a(P1), .b(2'b11), .eq(comparator_10_eq));  // open: gt, lt
  Multiplexer #(.width(2)) multiplexer_7 (
    .in0(multiplexer_6_out), .in1(2'b11), .out(multiplexer_7_out), .sel(and_4_out));
  and W1 (W1_out, comparator_3_eq, nor_1_out);
  and W2 (W2_out, comparator_4_eq, nor_1_out);
  Comparator #(.mode("unsigned"), .width(2)) comparator_11 (.a(P2), .b(2'b10), .eq(comparator_11_eq));  // open: gt, lt
  and and_3 (and_3_out, comparator_10_eq, comparator_11_eq);
  Comparator #(.mode("unsigned"), .width(2)) comparator_12 (.a(P1), .b(2'b00), .eq(comparator_12_eq));  // open: gt, lt
  or or_2 (or_2_out, comparator_12_eq, comparator_13_eq);
  or or_3 (or_3_out, comparator_6_eq, comparator_9_eq);
  Comparator #(.mode("unsigned"), .width(2)) comparator_13 (.a(P2), .b(2'b00), .eq(comparator_13_eq));  // open: gt, lt
  not not_1 (not_1_out, or_2_out);
  and and_4 (and_4_out, not_1_out, comparator_14_eq);
  Multiplexer multiplexer_8 (.in0(W1_out), .in1(1'b0), .out(WIN1), .sel(START));
  Multiplexer multiplexer_9 (.in0(W2_out), .in1(1'b0), .out(WIN2), .sel(START));
  Multiplexer multiplexer_10 (.in0(or_3_out), .in1(1'b0), .out(INVALID), .sel(START));
  Comparator #(.mode("unsigned"), .width(2)) comparator_14 (.a(P2), .b(P1), .eq(comparator_14_eq));  // open: gt, lt

  // Notes on the sheet:
  //   PLA AD HOC
  //   draw
  //   invalid_1
  //   MOVE CHECK
  //   invalid_2
  //   SIGNALS OUTPUT
  //   O: match winner (no move check)
endmodule

module set_total_manche (
  input  CLK,
  input  START,
  input  [1:0] P1,
  input  [1:0] P2,
  output [4:0] TO_PLAY
);

  wire adder_1_cout;
  wire [4:0] adder_1_out, adder_2_out, multiplexer_1_out, multiplexer_2_out, multiplexer_3_out;

  Multiplexer #(.select(2), .width(5)) multiplexer_1 (
    .in0({5{1'b0}}), .in1(5'b00100), .in2(5'b01000), .in3(5'b01100), .out(multiplexer_1_out), .sel(P1));
  Adder #(.width(5)) adder_1 (
    .a(multiplexer_2_out), .b(multiplexer_1_out), .out(adder_1_out), .cout(adder_1_cout));  // open: cin
  Multiplexer #(.select(2), .width(5)) multiplexer_2 (
    .in0({5{1'b0}}), .in1(5'b00001), .in2(5'b00010), .in3(5'b00011), .out(multiplexer_2_out), .sel(P2));
  Adder #(.width(5)) adder_2 (.a(adder_1_out), .b(5'b00100), .out(adder_2_out));  // open: cin, cout
  Multiplexer #(.width(5)) multiplexer_3 (.in0(TO_PLAY), .in1(adder_2_out), .out(multiplexer_3_out), .sel(START));
  Register #(.width(5)) FINAL (.D(multiplexer_3_out), .Q(TO_PLAY), .clk(CLK));  // open: en, clr
endmodule

module game_count (
  input  CLK,
  input  START,
  input  INVALID,
  output [4:0] PLAYED
);

  wire [4:0] adder_1_out, multiplexer_1_out, multiplexer_2_out;

  Adder #(.width(5)) adder_1 (.a(PLAYED), .b(5'b00001), .out(adder_1_out));  // open: cin, cout
  Multiplexer #(.width(5)) multiplexer_1 (.in0(adder_1_out), .in1(PLAYED), .out(multiplexer_1_out), .sel(INVALID));
  Multiplexer #(.width(5)) multiplexer_2 (
    .in0(multiplexer_1_out), .in1({5{1'b0}}), .out(multiplexer_2_out), .sel(START));
  Register #(.width(5)) PLAYED_M (.D(multiplexer_2_out), .Q(PLAYED), .clk(CLK));  // open: en, clr
endmodule

module game_adv (
  input  CLK,
  input  INVALID,
  input  WIN1,
  input  WIN2,
  input  START,
  output ADV1,
  output ADV2,
  output DRAW,
  output [4:0] ADV
);

  wire [4:0] adder_1_out, adder_2_out, multiplexer_1_out, multiplexer_2_out, multiplexer_3_out,
       multiplexer_4_out, multiplexer_5_out, multiplexer_6_out, multiplexer_7_out, subtractor_1_out,
       subtractor_2_out, WCOUNT_1_q, WCOUNT_2_q;

  Adder #(.width(5)) adder_1 (.a(WCOUNT_1_q), .b(5'b00001), .out(adder_1_out));  // open: cin, cout
  Adder #(.width(5)) adder_2 (.a(WCOUNT_2_q), .b(5'b00001), .out(adder_2_out));  // open: cin, cout
  Multiplexer #(.width(5)) multiplexer_1 (.in0(WCOUNT_1_q), .in1(adder_1_out), .out(multiplexer_1_out), .sel(WIN1));
  Multiplexer #(.width(5)) multiplexer_2 (
    .in0(multiplexer_1_out), .in1({5{1'b0}}), .out(multiplexer_2_out), .sel(START));
  Multiplexer #(.width(5)) multiplexer_3 (
    .in0(multiplexer_2_out), .in1(WCOUNT_1_q), .out(multiplexer_3_out), .sel(INVALID));
  Multiplexer #(.width(5)) multiplexer_4 (.in0(WCOUNT_2_q), .in1(adder_2_out), .out(multiplexer_4_out), .sel(WIN2));
  Multiplexer #(.width(5)) multiplexer_5 (
    .in0(multiplexer_4_out), .in1({5{1'b0}}), .out(multiplexer_5_out), .sel(START));
  Multiplexer #(.width(5)) multiplexer_6 (
    .in0(multiplexer_5_out), .in1(WCOUNT_2_q), .out(multiplexer_6_out), .sel(INVALID));
  Register #(.width(5)) WCOUNT_1 (.D(multiplexer_3_out), .Q(WCOUNT_1_q), .clk(CLK));  // open: en, clr
  Register #(.width(5)) WCOUNT_2 (.D(multiplexer_6_out), .Q(WCOUNT_2_q), .clk(CLK));  // open: en, clr
  Comparator #(.mode("unsigned"), .width(5)) comparator_1 (.a(WCOUNT_1_q), .b(WCOUNT_2_q), .gt(ADV1));  // open: eq, lt
  Comparator #(.mode("unsigned"), .width(5)) comparator_2 (.a(WCOUNT_1_q), .b(WCOUNT_2_q), .eq(DRAW));  // open: gt, lt
  Subtractor #(.width(5)) subtractor_1 (.a(WCOUNT_1_q), .b(WCOUNT_2_q), .out(subtractor_1_out));  // open: bin, bout
  Subtractor #(.width(5)) subtractor_2 (.a(WCOUNT_2_q), .b(WCOUNT_1_q), .out(subtractor_2_out));  // open: bin, bout
  nor nor_1 (ADV2, ADV1, DRAW);
  Multiplexer #(.width(5)) multiplexer_7 (.in0(subtractor_1_out), .in1({5{1'b0}}), .out(multiplexer_7_out), .sel(DRAW));
  Multiplexer #(.width(5)) multiplexer_8 (.in0(subtractor_2_out), .in1(multiplexer_7_out), .out(ADV), .sel(ADV1));

  // Notes on the sheet:
  //   OTTIMIZZABILE
endmodule

module end_game (
  input  [4:0] MATCH_ADV,
  input  DRAW,
  input  ADV1,
  input  ADV2,
  input  [4:0] PLAYED,
  input  [4:0] TO_PLAY,
  output GAME1,
  output GAME2,
  output GAMED,
  output STOP
);

  wire and_1_out, comparator_1_gt, comparator_2_eq, comparator_3_gt, or_1_out;

  Comparator #(.width(5)) comparator_1 (.a(PLAYED), .b(5'b00011), .gt(comparator_1_gt));  // open: eq, lt
  Comparator #(.width(5)) comparator_2 (.a(TO_PLAY), .b(PLAYED), .eq(comparator_2_eq));  // open: gt, lt
  or or_1 (or_1_out, comparator_1_gt, comparator_2_eq);
  Comparator #(.width(5)) comparator_3 (.a(MATCH_ADV), .b(5'b00001), .gt(comparator_3_gt));  // open: eq, lt
  and and_1 (and_1_out, comparator_3_gt, comparator_1_gt);
  or or_2 (STOP, and_1_out, comparator_2_eq);
  and and_2 (GAME1, ADV2, or_1_out);
  and and_3 (GAME2, ADV1, or_1_out);
  and and_4 (GAMED, or_1_out, DRAW);

  // Notes on the sheet:
  //   END GAME
endmodule

module match_winner_2 (
  input  [1:0] P1,
  input  [1:0] P2,
  input  START,
  input  CLK,
  output WIN1,
  output WIN2,
  output INVALID
);

  wire and_1_out, and_2_out, and_3_out, and_4_out, comparator_1_eq, comparator_2_eq, comparator_3_eq,
       comparator_4_eq, comparator_5_eq, comparator_6_eq, comparator_7_eq, comparator_8_eq, comparator_9_eq,
       comparator_10_eq, comparator_11_eq, comparator_12_eq, comparator_13_eq, comparator_14_eq,
       comparator_15_eq, nor_1_out, not_2_out, or_1_out, or_2_out, or_3_out, W1_out, W2_out;
  wire [1:0] multiplexer_1_out, multiplexer_2_out, multiplexer_3_out, multiplexer_4_out, multiplexer_5_out,
       multiplexer_6_out, multiplexer_7_out, multiplexer_8_out, multiplexer_9_out, not_1_out, register_1_q,
       register_2_q;

  Comparator #(.mode("unsigned"), .width(2)) comparator_1 (.a(P1), .b(2'b01), .eq(comparator_1_eq));  // open: gt, lt
  Multiplexer #(.select(2), .width(2)) multiplexer_1 (
    .in0(register_1_q), .in1(multiplexer_9_out), .in2(multiplexer_9_out), .in3(2'b00),
    .out(multiplexer_1_out), .sel(multiplexer_9_out));
  Multiplexer #(.width(2)) multiplexer_2 (.in0(multiplexer_1_out), .in1(2'b00), .out(multiplexer_2_out), .sel(START));
  Comparator #(.mode("unsigned"), .width(2)) comparator_2 (.a(P2), .b(2'b11), .eq(comparator_2_eq));  // open: gt, lt
  and and_1 (and_1_out, comparator_1_eq, comparator_2_eq);
  Register #(.width(2)) register_1 (.D(multiplexer_2_out), .Q(register_1_q), .clk(CLK));  // open: en, clr
  Comparator #(.mode("unsigned"), .width(2)) comparator_3 (
    .a(multiplexer_7_out), .b(2'b01), .eq(comparator_3_eq));  // open: gt, lt
  Comparator #(.mode("unsigned"), .width(2)) comparator_4 (
    .a(multiplexer_7_out), .b(2'b10), .eq(comparator_4_eq));  // open: gt, lt
  Comparator #(.mode("unsigned"), .width(2)) comparator_5 (
    .a(multiplexer_7_out), .b(2'b11), .eq(comparator_5_eq));  // open: gt, lt
  Comparator #(.mode("unsigned"), .width(2)) comparator_6 (
    .a(multiplexer_7_out), .b(2'b00), .eq(comparator_6_eq));  // open: gt, lt
  Comparator #(.mode("unsigned"), .width(2)) comparator_7 (.a(P1), .b(2'b10), .eq(comparator_7_eq));  // open: gt, lt
  Multiplexer #(.select(2), .width(2)) multiplexer_3 (
    .in0(register_2_q), .in1(P1), .in2(P2), .in3(register_2_q), .out(multiplexer_3_out),
    .sel(multiplexer_9_out));
  Multiplexer #(.width(2)) multiplexer_4 (.in0(multiplexer_3_out), .in1(2'b00), .out(multiplexer_4_out), .sel(START));
  Comparator #(.mode("unsigned"), .width(2)) comparator_8 (.a(P2), .b(2'b01), .eq(comparator_8_eq));  // open: gt, lt
  and and_2 (and_2_out, comparator_7_eq, comparator_8_eq);
  or or_1 (or_1_out, and_1_out, and_2_out, and_3_out);
  Multiplexer #(.width(2)) multiplexer_5 (.in0(2'b10), .in1(2'b01), .out(multiplexer_5_out), .sel(or_1_out));
  nor nor_1 (nor_1_out, comparator_5_eq, comparator_6_eq);
  Register #(.width(2)) register_2 (.D(multiplexer_4_out), .Q(register_2_q), .clk(CLK));  // open: en, clr
  Multiplexer #(.width(2)) multiplexer_6 (
    .in0(multiplexer_5_out), .in1(2'b00), .out(multiplexer_6_out), .sel(or_2_out));
  Comparator #(.mode("unsigned"), .width(2)) comparator_9 (.a(P1), .b(2'b11), .eq(comparator_9_eq));  // open: gt, lt
  Multiplexer #(.width(2)) multiplexer_7 (
    .in0(multiplexer_6_out), .in1(2'b11), .out(multiplexer_7_out), .sel(and_4_out));
  and W1 (W1_out, comparator_3_eq, nor_1_out);
  and W2 (W2_out, comparator_4_eq, nor_1_out);
  Comparator #(.mode("unsigned"), .width(2)) comparator_10 (.a(P2), .b(2'b10), .eq(comparator_10_eq));  // open: gt, lt
  and and_3 (and_3_out, comparator_9_eq, comparator_10_eq);
  assign not_1_out = ~register_2_q;  // NOT_Gate not_1, 2 bits wide
  Multiplexer #(.select(2), .width(2)) multiplexer_8 (
    .in0(not_1_out), .in1(P1), .in2(P2), .in3(not_1_out), .out(multiplexer_8_out), .sel(register_1_q));
  Comparator #(.mode("unsigned"), .width(2)) comparator_11 (.a(P1), .b(2'b00), .eq(comparator_11_eq));  // open: gt, lt
  Comparator #(.width(2)) comparator_12 (.a(2'b00), .b(multiplexer_9_out), .eq(comparator_12_eq));  // open: gt, lt
  or or_2 (or_2_out, comparator_11_eq, comparator_14_eq);
  or or_3 (or_3_out, comparator_6_eq, comparator_12_eq);
  Multiplexer #(.width(2)) multiplexer_9 (
    .in0(multiplexer_7_out), .in1(2'b00), .out(multiplexer_9_out), .sel(comparator_13_eq));
  Comparator #(.width(2)) comparator_13 (
    .a(multiplexer_8_out), .b(register_2_q), .eq(comparator_13_eq));  // open: gt, lt
  Comparator #(.mode("unsigned"), .width(2)) comparator_14 (.a(P2), .b(2'b00), .eq(comparator_14_eq));  // open: gt, lt
  not not_2 (not_2_out, or_2_out);
  and and_4 (and_4_out, not_2_out, comparator_15_eq);
  Multiplexer multiplexer_10 (.in0(W1_out), .in1(1'b0), .out(WIN1), .sel(START));
  Multiplexer multiplexer_11 (.in0(W2_out), .in1(1'b0), .out(WIN2), .sel(START));
  Multiplexer multiplexer_12 (.in0(or_3_out), .in1(1'b0), .out(INVALID), .sel(START));
  Comparator #(.mode("unsigned"), .width(2)) comparator_15 (.a(P2), .b(P1), .eq(comparator_15_eq));  // open: gt, lt

  // Notes on the sheet:
  //   PLA AD HOC
  //   draw
  //   invalid_1
  //   SIGNALS OUTPUT
  //   O: match winner (no move check)
  //   OTTIMIZZABILE
endmodule
